// Logisim project lab3_part1.circ as structural Verilog: 1 circuit, main circuit main
module main (
  input  [9:0] A,
  output Y
);

  Multiplexer #(.enable("false"), .select(3)) multiplexer_1 (
    .in0(A[0]), .in1(A[1]), .in2(A[2]), .in3(A[3]), .in4(A[4]), .in5(A[5]), .in6(A[6]), .in7(1'b0), .out(Y),
    .sel(A[9:7]));

  // Notes on the sheet:
  //   top: A[0]
  //   s1
  //   s2
  //   s0
endmodule
