// Logisim project lab3_part2.circ as structural Verilog: 2 circuits, main circuit main
module main (
  input  [3:0] B,
  input  [3:0] A,
  input  C_in,
  output C_out,
  output [3:0] S
);

  wire fulladder_2_c_out, fulladder_3_c_out, fulladder_4_c_out;

  fullAdder fulladder_1 (.c_in(fulladder_2_c_out), .a(A[3]), .b(B[3]), .s(S[3]), .c_out(C_out));
  fullAdder fulladder_2 (.c_in(fulladder_3_c_out), .a(A[2]), .b(B[2]), .s(S[2]), .c_out(fulladder_2_c_out));
  fullAdder fulladder_3 (.c_in(fulladder_4_c_out), .a(A[1]), .b(B[1]), .s(S[1]), .c_out(fulladder_3_c_out));
  fullAdder fulladder_4 (.c_in(C_in), .a(A[0]), .b(B[0]), .s(S[0]), .c_out(fulladder_4_c_out));
endmodule

module fullAdder (
  input  c_in,
  input  a,
  input  b,
  output s,
  output c_out
);

  wire and_1_out, and_2_out, xor_1_out;

  xor xor_1 (xor_1_out, a, b);
  and and_1 (and_1_out, a, b);
  and and_2 (and_2_out, c_in, xor_1_out);
  xor xor_2 (s, c_in, xor_1_out);
  or or_1 (c_out, and_2_out, and_1_out);
endmodule
