// Logisim project lab1_part1.circ as structural Verilog: 1 circuit, main circuit main
module main (
  input  y,
  input  s,
  input  x,
  output f
);

  wire and_1_out, and_2_out, not_1_out;

  not not_1 (not_1_out, s);
  and and_1 (and_1_out, y, s);
  and and_2 (and_2_out, not_1_out, x);
  or or_1 (f, and_1_out, and_2_out);

  // Notes on the sheet:
  //   xs’+ys
endmodule
