// Logisim project lab1_part2.circ as structural Verilog: 1 circuit, main circuit main
module main (
  input  A,
  input  B,
  input  C,
  input  A1,
  input  B1,
  input  C1,
  output f,
  output f1
);

  wire and_1_out, not_1_out, not_2_out, not_3_out, not_4_out, or_1_out, or_2_out;

  not not_1 (not_1_out, A1);
  not not_2 (not_2_out, B1);
  or or_1 (or_1_out, A, B);
  not not_3 (not_3_out, B);
  not not_4 (not_4_out, or_1_out);
  and and_1 (and_1_out, not_3_out, C);
  or or_2 (or_2_out, not_1_out, C1);
  and and_2 (f1, not_2_out, or_2_out);
  or or_3 (f, not_4_out, and_1_out);

  // Notes on the sheet:
  //   OR
  //   AND
  //   Original Circuit
  //   Optimal Circuit
  //   OR
  //   b’(a’+c)
  //   (a + b)’ + cb’ 
endmodule
