// Logisim project part1.circ as structural Verilog: 9 circuits, main circuit sevenSegment
module sevenSegment (
  input  c3,
  input  c2,
  input  c1,
  input  c0,
  output y0,
  output y1,
  output y2,
  output y3,
  output y4,
  output y5,
  output y6
);

  Segment0 s0 (.A(c3), .B(c2), .C(c1), .D(c0), .Y(y0));
  Segment1 s1 (.A(c3), .B(c2), .C(c1), .D(c0), .Y(y1));
  Segment2 s2 (.A(c3), .B(c2), .C(c1), .D(c0), .Y(y2));
  Segment3 s3 (.A(c3), .B(c2), .C(c1), .D(c0), .Y(y3));
  Segment4 s4 (.A(c3), .B(c2), .C(c1), .D(c0), .Y(y4));
  Segment5 s5 (.A(c3), .B(c2), .C(c1), .D(c0), .Y(y5));
  Segment6 s6 (.A(c3), .B(c2), .C(c1), .D(c0), .Y(y6));
  _7_Segment_Display Y (.g(y6), .f(y5), .a(y0), .b(y1), .e(y4), .d(y3), .c(y2));  // open: dp
endmodule

module Segment0 (
  input  A,
  input  B,
  input  C,
  input  D,
  output Y
);

  wire and_1_out, and_2_out, and_3_out, and_4_out, and_5_out, and_6_out, not_1_out, not_2_out, not_3_out,
       not_4_out;

  not not_1 (not_1_out, A);
  not not_2 (not_2_out, B);
  not not_3 (not_3_out, C);
  not not_4 (not_4_out, D);
  and and_1 (and_1_out, not_1_out, C);
  and and_2 (and_2_out, not_2_out, not_4_out);
  and and_3 (and_3_out, B, C);
  and and_4 (and_4_out, A, not_4_out);
  and and_5 (and_5_out, not_1_out, B, D);
  and and_6 (and_6_out, A, not_2_out, not_3_out);
  or or_1 (Y, and_1_out, and_2_out, and_3_out, and_4_out, and_5_out, and_6_out);
endmodule

module Segment1 (
  input  A,
  input  B,
  input  C,
  input  D,
  output Y
);

  wire and_1_out, and_2_out, and_3_out, and_4_out, and_5_out, not_1_out, not_2_out, not_3_out, not_4_out;

  not not_1 (not_1_out, A);
  not not_2 (not_2_out, B);
  not not_3 (not_3_out, C);
  not not_4 (not_4_out, D);
  and and_1 (and_1_out, not_1_out, not_2_out);
  and and_2 (and_2_out, not_2_out, not_4_out);
  and and_3 (and_3_out, not_1_out, not_3_out, not_4_out);
  and and_4 (and_4_out, not_1_out, C, D);
  and and_5 (and_5_out, A, not_3_out, D);
  or or_1 (Y, and_1_out, and_2_out, and_3_out, and_4_out, and_5_out);
endmodule

module Segment2 (
  input  A,
  input  B,
  input  C,
  input  D,
  output Y
);

  wire and_1_out, and_2_out, and_3_out, and_4_out, and_5_out, not_1_out, not_2_out, not_3_out;

  not not_1 (not_1_out, A);
  not not_2 (not_2_out, B);
  not not_3 (not_3_out, C);
  and and_1 (and_1_out, not_1_out, not_3_out);
  and and_2 (and_2_out, not_1_out, D);
  and and_3 (and_3_out, not_3_out, D);
  and and_4 (and_4_out, not_1_out, B);
  and and_5 (and_5_out, A, not_2_out);
  or or_1 (Y, and_1_out, and_2_out, and_3_out, and_4_out, and_5_out);
endmodule

module Segment3 (
  input  A,
  input  B,
  input  C,
  input  D,
  output Y
);

  wire and_1_out, and_2_out, and_3_out, and_4_out, and_5_out, not_1_out, not_2_out, not_3_out, not_4_out;

  not not_1 (not_1_out, A);
  not not_2 (not_2_out, B);
  not not_3 (not_3_out, C);
  not not_4 (not_4_out, D);
  and and_1 (and_1_out, not_1_out, not_2_out, not_4_out);
  and and_2 (and_2_out, not_2_out, C, D);
  and and_3 (and_3_out, B, not_3_out, D);
  and and_4 (and_4_out, B, C, not_4_out);
  and and_5 (and_5_out, A, not_3_out, not_4_out);
  or or_1 (Y, and_1_out, and_2_out, and_3_out, and_4_out, and_5_out);
endmodule

module Segment4 (
  input  A,
  input  B,
  input  C,
  input  D,
  output Y
);

  wire and_1_out, and_2_out, and_3_out, and_4_out, not_1_out, not_2_out;

  not not_1 (not_1_out, B);
  not not_2 (not_2_out, D);
  and and_1 (and_1_out, A, C);
  and and_2 (and_2_out, not_1_out, not_2_out);
  and and_3 (and_3_out, C, not_2_out);
  and and_4 (and_4_out, A, B);
  or or_1 (Y, and_1_out, and_2_out, and_3_out, and_4_out);
endmodule

module Segment5 (
  input  A,
  input  B,
  input  C,
  input  D,
  output Y
);

  wire and_1_out, and_2_out, and_3_out, and_4_out, and_5_out, not_1_out, not_2_out, not_3_out, not_4_out;

  not not_1 (not_1_out, A);
  not not_2 (not_2_out, B);
  not not_3 (not_3_out, C);
  not not_4 (not_4_out, D);
  and and_1 (and_1_out, A, not_2_out);
  and and_2 (and_2_out, A, C);
  and and_3 (and_3_out, not_3_out, not_4_out);
  and and_4 (and_4_out, B, not_4_out);
  and and_5 (and_5_out, not_1_out, B, not_3_out);
  or or_1 (Y, and_1_out, and_2_out, and_3_out, and_4_out, and_5_out);
endmodule

module Segment6 (
  input  A,
  input  B,
  input  C,
  input  D,
  output Y
);

  wire and_1_out, and_2_out, and_3_out, and_4_out, and_5_out, not_1_out, not_2_out, not_3_out, not_4_out;

  not not_1 (not_1_out, A);
  not not_2 (not_2_out, B);
  not not_3 (not_3_out, C);
  not not_4 (not_4_out, D);
  and and_1 (and_1_out, A, not_2_out);
  and and_2 (and_2_out, not_2_out, C);
  and and_3 (and_3_out, C, not_4_out);
  and and_4 (and_4_out, A, D);
  and and_5 (and_5_out, not_1_out, B, not_3_out);
  or or_1 (Y, and_1_out, and_2_out, and_3_out, and_4_out, and_5_out);
endmodule

module main (
  input  Enable,
  input  Clock,
  input  Clear_b
);

  wire and_1_out, and_2_out, and_3_out, and_4_out, and_5_out, and_6_out, and_7_out, not_1_out,
       sevensegment_1_y0, sevensegment_1_y1, sevensegment_1_y2, sevensegment_1_y3, sevensegment_1_y4,
       sevensegment_1_y5, sevensegment_1_y6, sevensegment_2_y0, sevensegment_2_y1, sevensegment_2_y2,
       sevensegment_2_y3, sevensegment_2_y4, sevensegment_2_y5, sevensegment_2_y6, t_ff_1_q, t_ff_2_q,
       t_ff_3_q, t_ff_4_q, t_ff_5_q, t_ff_6_q, t_ff_7_q, t_ff_8_q;

  not not_1 (not_1_out, Clear_b);
  T_Flip_Flop t_ff_1 (.T(Enable), .clk(Clock), .Q(t_ff_1_q), .reset(not_1_out));  // open: Qn, preset
  LED LED0 (.in(t_ff_1_q));
  and and_1 (and_1_out, Enable, t_ff_1_q);
  T_Flip_Flop t_ff_2 (.T(and_1_out), .clk(Clock), .Q(t_ff_2_q), .reset(not_1_out));  // open: Qn, preset
  LED LED1 (.in(t_ff_2_q));
  and and_2 (and_2_out, and_1_out, t_ff_2_q);
  T_Flip_Flop t_ff_3 (.T(and_2_out), .clk(Clock), .Q(t_ff_3_q), .reset(not_1_out));  // open: Qn, preset
  LED LED2 (.in(t_ff_3_q));
  and and_3 (and_3_out, and_2_out, t_ff_3_q);
  T_Flip_Flop t_ff_4 (.T(and_3_out), .clk(Clock), .Q(t_ff_4_q), .reset(not_1_out));  // open: Qn, preset
  LED LED3 (.in(t_ff_4_q));
  sevenSegment sevensegment_1 (
    .c3(t_ff_8_q), .c2(t_ff_7_q), .c1(t_ff_6_q), .c0(t_ff_5_q), .y0(sevensegment_1_y0),
    .y1(sevensegment_1_y1), .y2(sevensegment_1_y2), .y3(sevensegment_1_y3), .y4(sevensegment_1_y4),
    .y5(sevensegment_1_y5), .y6(sevensegment_1_y6));
  sevenSegment sevensegment_2 (
    .c3(t_ff_4_q), .c2(t_ff_3_q), .c1(t_ff_2_q), .c0(t_ff_1_q), .y0(sevensegment_2_y0),
    .y1(sevensegment_2_y1), .y2(sevensegment_2_y2), .y3(sevensegment_2_y3), .y4(sevensegment_2_y4),
    .y5(sevensegment_2_y5), .y6(sevensegment_2_y6));
  and and_4 (and_4_out, and_3_out, t_ff_4_q);
  T_Flip_Flop t_ff_5 (.T(and_4_out), .clk(Clock), .Q(t_ff_5_q), .reset(not_1_out));  // open: Qn, preset
  LED LED4 (.in(t_ff_5_q));
  and and_5 (and_5_out, and_4_out, t_ff_5_q);
  _7_Segment_Display u_7_segment_display_1 (
    .g(sevensegment_1_y6), .f(sevensegment_1_y5), .a(sevensegment_1_y0), .b(sevensegment_1_y1),
    .e(sevensegment_1_y4), .d(sevensegment_1_y3), .c(sevensegment_1_y2));  // open: dp
  T_Flip_Flop t_ff_6 (.T(and_5_out), .clk(Clock), .Q(t_ff_6_q), .reset(not_1_out));  // open: Qn, preset
  _7_Segment_Display u_7_segment_display_2 (
    .g(sevensegment_2_y6), .f(sevensegment_2_y5), .a(sevensegment_2_y0), .b(sevensegment_2_y1),
    .e(sevensegment_2_y4), .d(sevensegment_2_y3), .c(sevensegment_2_y2));  // open: dp
  LED LED5 (.in(t_ff_6_q));
  and and_6 (and_6_out, and_5_out, t_ff_6_q);
  T_Flip_Flop t_ff_7 (.T(and_6_out), .clk(Clock), .Q(t_ff_7_q), .reset(not_1_out));  // open: Qn, preset
  LED LED6 (.in(t_ff_7_q));
  and and_7 (and_7_out, and_6_out, t_ff_7_q);
  T_Flip_Flop t_ff_8 (.T(and_7_out), .clk(Clock), .Q(t_ff_8_q), .reset(not_1_out));  // open: Qn, preset
  LED LED7 (.in(t_ff_8_q));
endmodule
