// Logisim project part2.circ as structural Verilog: 11 circuits, main circuit main
module main (
  input  SW_0,
  input  SW_1,
  input  Enable,
  input  Clear_b
);

  wire Clk_out, displaycounter_1_y0, displaycounter_1_y1, displaycounter_1_y2, displaycounter_1_y3,
       displaycounter_1_y4, displaycounter_1_y5, displaycounter_1_y6, ratedivider_1_clk_out;

  Clock Clk (.out(Clk_out));
  RateDivider ratedivider_1 (.Clk(Clk_out), .SW_0(SW_0), .SW_1(SW_1), .Clk_out(ratedivider_1_clk_out));
  DisplayCounter displaycounter_1 (
    .clear_b(Clear_b), .enable(Enable), .clk(ratedivider_1_clk_out), .y0(displaycounter_1_y0),
    .y1(displaycounter_1_y1), .y2(displaycounter_1_y2), .y3(displaycounter_1_y3), .y4(displaycounter_1_y4),
    .y5(displaycounter_1_y5), .y6(displaycounter_1_y6));
  _7_Segment_Display HEX_0 (
    .g(displaycounter_1_y6), .f(displaycounter_1_y5), .a(displaycounter_1_y0), .b(displaycounter_1_y1),
    .e(displaycounter_1_y4), .d(displaycounter_1_y3), .c(displaycounter_1_y2));  // open: dp
endmodule

module RateDivider (
  input  Clk,
  input  SW_0,
  input  SW_1,
  output Clk_out
);

  wire and_1_out, and_5_out, and_6_out, not_1_out, not_2_out, not_3_out, not_4_out;
  wire [6:4] and_2_out;
  wire [7:0] counter_1_q, not_5_out;

  not not_1 (not_1_out, SW_0);
  not not_2 (not_2_out, SW_1);
  not not_3 (not_3_out, SW_1);
  not not_4 (not_4_out, SW_0);
  and and_1 (and_1_out, not_1_out, not_2_out);
  and and_2 (and_2_out[4], SW_0, not_3_out);
  and and_3 (and_2_out[5], not_4_out, SW_1);
  and and_4 (and_2_out[6], SW_0, SW_1);
  and and_5 (and_5_out, Clk, and_1_out);
  Counter counter_1 (
    .load(and_6_out), .up(1'b0), .clk(Clk), .D({1'b0, and_2_out, 4'b0000}), .Q(counter_1_q));  // open: clr, count, carry
  assign not_5_out = ~counter_1_q;  // NOT_Gate not_5, 8 bits wide
  and and_6 (and_6_out, not_5_out[0], not_5_out[1], not_5_out[2], not_5_out[3], not_5_out[4], not_5_out[5], not_5_out[6], not_5_out[7]);
  xor xor_1 (Clk_out, and_5_out, and_6_out);
endmodule

module DisplayCounter (
  input  clear_b,
  input  enable,
  input  clk,
  output y0,
  output y1,
  output y2,
  output y3,
  output y4,
  output y5,
  output y6
);

  wire not_1_out;
  wire [3:0] counter_1_q;

  not not_1 (not_1_out, enable);
  Counter #(.max('hf), .width(4)) counter_1 (
    .clr(clear_b), .load(not_1_out), .up(1'b1), .clk(clk), .D(counter_1_q), .Q(counter_1_q));  // open: count, carry
  sevenSegment sevensegment_1 (
    .c3(counter_1_q[3]), .c2(counter_1_q[2]), .c1(counter_1_q[1]), .c0(counter_1_q[0]), .y0(y0), .y1(y1),
    .y2(y2), .y3(y3), .y4(y4), .y5(y5), .y6(y6));
endmodule

module sevenSegment (
  input  c3,
  input  c2,
  input  c1,
  input  c0,
  output y0,
  output y1,
  output y2,
  output y3,
  output y4,
  output y5,
  output y6
);

  Segment0 s0 (.A(c3), .B(c2), .C(c1), .D(c0), .Y(y0));
  Segment1 s1 (.A(c3), .B(c2), .C(c1), .D(c0), .Y(y1));
  Segment2 s2 (.A(c3), .B(c2), .C(c1), .D(c0), .Y(y2));
  Segment3 s3 (.A(c3), .B(c2), .C(c1), .D(c0), .Y(y3));
  Segment4 s4 (.A(c3), .B(c2), .C(c1), .D(c0), .Y(y4));
  Segment5 s5 (.A(c3), .B(c2), .C(c1), .D(c0), .Y(y5));
  Segment6 s6 (.A(c3), .B(c2), .C(c1), .D(c0), .Y(y6));
  _7_Segment_Display Y (.g(y6), .f(y5), .a(y0), .b(y1), .e(y4), .d(y3), .c(y2));  // open: dp
endmodule

module Segment0 (
  input  A,
  input  B,
  input  C,
  input  D,
  output Y
);

  wire and_1_out, and_2_out, and_3_out, and_4_out, and_5_out, and_6_out, not_1_out, not_2_out, not_3_out,
       not_4_out;

  not not_1 (not_1_out, A);
  not not_2 (not_2_out, B);
  not not_3 (not_3_out, C);
  not not_4 (not_4_out, D);
  and and_1 (and_1_out, not_1_out, C);
  and and_2 (and_2_out, not_2_out, not_4_out);
  and and_3 (and_3_out, B, C);
  and and_4 (and_4_out, A, not_4_out);
  and and_5 (and_5_out, not_1_out, B, D);
  and and_6 (and_6_out, A, not_2_out, not_3_out);
  or or_1 (Y, and_1_out, and_2_out, and_3_out, and_4_out, and_5_out, and_6_out);
endmodule

module Segment1 (
  input  A,
  input  B,
  input  C,
  input  D,
  output Y
);

  wire and_1_out, and_2_out, and_3_out, and_4_out, and_5_out, not_1_out, not_2_out, not_3_out, not_4_out;

  not not_1 (not_1_out, A);
  not not_2 (not_2_out, B);
  not not_3 (not_3_out, C);
  not not_4 (not_4_out, D);
  and and_1 (and_1_out, not_1_out, not_2_out);
  and and_2 (and_2_out, not_2_out, not_4_out);
  and and_3 (and_3_out, not_1_out, not_3_out, not_4_out);
  and and_4 (and_4_out, not_1_out, C, D);
  and and_5 (and_5_out, A, not_3_out, D);
  or or_1 (Y, and_1_out, and_2_out, and_3_out, and_4_out, and_5_out);
endmodule

module Segment2 (
  input  A,
  input  B,
  input  C,
  input  D,
  output Y
);

  wire and_1_out, and_2_out, and_3_out, and_4_out, and_5_out, not_1_out, not_2_out, not_3_out;

  not not_1 (not_1_out, A);
  not not_2 (not_2_out, B);
  not not_3 (not_3_out, C);
  and and_1 (and_1_out, not_1_out, not_3_out);
  and and_2 (and_2_out, not_1_out, D);
  and and_3 (and_3_out, not_3_out, D);
  and and_4 (and_4_out, not_1_out, B);
  and and_5 (and_5_out, A, not_2_out);
  or or_1 (Y, and_1_out, and_2_out, and_3_out, and_4_out, and_5_out);
endmodule

module Segment3 (
  input  A,
  input  B,
  input  C,
  input  D,
  output Y
);

  wire and_1_out, and_2_out, and_3_out, and_4_out, and_5_out, not_1_out, not_2_out, not_3_out, not_4_out;

  not not_1 (not_1_out, A);
  not not_2 (not_2_out, B);
  not not_3 (not_3_out, C);
  not not_4 (not_4_out, D);
  and and_1 (and_1_out, not_1_out, not_2_out, not_4_out);
  and and_2 (and_2_out, not_2_out, C, D);
  and and_3 (and_3_out, B, not_3_out, D);
  and and_4 (and_4_out, B, C, not_4_out);
  and and_5 (and_5_out, A, not_3_out, not_4_out);
  or or_1 (Y, and_1_out, and_2_out, and_3_out, and_4_out, and_5_out);
endmodule

module Segment4 (
  input  A,
  input  B,
  input  C,
  input  D,
  output Y
);

  wire and_1_out, and_2_out, and_3_out, and_4_out, not_1_out, not_2_out;

  not not_1 (not_1_out, B);
  not not_2 (not_2_out, D);
  and and_1 (and_1_out, A, C);
  and and_2 (and_2_out, not_1_out, not_2_out);
  and and_3 (and_3_out, C, not_2_out);
  and and_4 (and_4_out, A, B);
  or or_1 (Y, and_1_out, and_2_out, and_3_out, and_4_out);
endmodule

module Segment5 (
  input  A,
  input  B,
  input  C,
  input  D,
  output Y
);

  wire and_1_out, and_2_out, and_3_out, and_4_out, and_5_out, not_1_out, not_2_out, not_3_out, not_4_out;

  not not_1 (not_1_out, A);
  not not_2 (not_2_out, B);
  not not_3 (not_3_out, C);
  not not_4 (not_4_out, D);
  and and_1 (and_1_out, A, not_2_out);
  and and_2 (and_2_out, A, C);
  and and_3 (and_3_out, not_3_out, not_4_out);
  and and_4 (and_4_out, B, not_4_out);
  and and_5 (and_5_out, not_1_out, B, not_3_out);
  or or_1 (Y, and_1_out, and_2_out, and_3_out, and_4_out, and_5_out);
endmodule

module Segment6 (
  input  A,
  input  B,
  input  C,
  input  D,
  output Y
);

  wire and_1_out, and_2_out, and_3_out, and_4_out, and_5_out, not_1_out, not_2_out, not_3_out, not_4_out;

  not not_1 (not_1_out, A);
  not not_2 (not_2_out, B);
  not not_3 (not_3_out, C);
  not not_4 (not_4_out, D);
  and and_1 (and_1_out, A, not_2_out);
  and and_2 (and_2_out, not_2_out, C);
  and and_3 (and_3_out, C, not_4_out);
  and and_4 (and_4_out, A, D);
  and and_5 (and_5_out, not_1_out, B, not_3_out);
  or or_1 (Y, and_1_out, and_2_out, and_3_out, and_4_out, and_5_out);
endmodule
