// Logisim project part3.circ as structural Verilog: 4 circuits, main circuit main
module main (
  input  SW_0,
  input  SW_1,
  input  SW_2,
  input  KEY_0,
  input  KEY_1
);

  wire Clk32Hz_out, ratedivider_1_clk_out, shiftregister_1_y;
  wire [13:0] lut_1_code;

  Clock Clk32Hz (.out(Clk32Hz_out));
  rateDivider ratedivider_1 (.Clk(Clk32Hz_out), .Clk_out(ratedivider_1_clk_out));
  LUT lut_1 (.S({SW_2, SW_1, SW_0}), .code(lut_1_code));
  shiftRegister shiftregister_1 (
    .reset(KEY_0), .enable(KEY_1), .clock(ratedivider_1_clk_out), .load(lut_1_code), .y(shiftregister_1_y));
  LED LEDR_0 (.in(shiftregister_1_y));
endmodule

module LUT (
  input  [2:0] S,
  output [13:0] code
);

  Multiplexer #(.enable("false"), .select(3), .width(14)) multiplexer_1 (
    .in0(14'ha80), .in1(14'he00), .in2(14'hae0), .in3(14'hab8), .in4(14'hbb8), .in5(14'heae), .in6(14'h1d77),
    .in7(14'heea), .out(code), .sel(S));

  // Notes on the sheet:
  //   s
  //   t
  //   u
  //   v
  //   w
  //   x
  //   y
  //   z
endmodule

module shiftRegister (
  input  reset,
  input  enable,
  input  clock,
  input  [13:0] load,
  output y
);

  wire d_ff_1_q, d_ff_1_qn;

  D_Flip_Flop d_ff_1 (.D(enable), .clk(clock), .Q(d_ff_1_q), .Qn(d_ff_1_qn));  // open: preset, reset
  // Shift_Register #(.length(14)) shift_register_1: pin names not known; wires that end beside it: reset, d_ff_1_qn, d_ff_1_q, clock, 1'b0, load[0], load[1], load[2], load[3], load[4], load[5], load[6], load[7], load[8], load[9], load[10], load[11]
endmodule

module rateDivider (
  input  Clk,
  output Clk_out
);

  wire [2:0] counter_1_q;

  Counter #(.max('h7), .width(3)) counter_1 (
    .load(1'b0), .up(1'b1), .clk(Clk), .D(3'b000), .Q(counter_1_q));  // open: clr, count, carry
  and and_1 (Clk_out, counter_1_q[0], counter_1_q[1], counter_1_q[2]);
endmodule
