// Logisim project part1.circ as structural Verilog: 1 circuit, main circuit main
module main (
  input  EN,
  input  Reset,
  input  OutputEN
);

  wire Clk_out, not_1_out, not_2_out, register_1_q, register_2_q;
  wire [3:0] counter_2_q, ram_1_dout, register_4_q;
  wire [4:0] counter_1_q, register_3_q;

  Clock Clk (.out(Clk_out));
  Register #(.width(1)) register_1 (.D(EN), .en(1'b1), .clk(Clk_out), .Q(register_1_q), .clr(Reset));
  Register #(.width(1)) register_2 (.D(OutputEN), .en(1'b1), .clk(Clk_out), .Q(register_2_q), .clr(Reset));
  not not_1 (not_1_out, register_1_q);
  Counter #(.max('h1f), .width(5)) counter_1 (
    .clr(Reset), .load(not_1_out), .up(1'b1), .clk(Clk_out), .D(counter_1_q), .Q(counter_1_q));  // open: count, carry
  Counter #(.max('hf), .width(4)) counter_2 (
    .clr(Reset), .load(not_2_out), .up(1'b1), .clk(Clk_out), .D(counter_2_q), .Q(counter_2_q));  // open: count, carry
  not not_2 (not_2_out, register_1_q);
  Register #(.width(5)) register_3 (.D(counter_1_q), .en(register_1_q), .clk(Clk_out), .Q(register_3_q), .clr(Reset));
  Register #(.width(4)) register_4 (.D(counter_2_q), .en(register_1_q), .clk(Clk_out), .Q(register_4_q), .clr(Reset));
  RAM #(.addrWidth(5), .dataWidth(4)) ram_1 (
    .addr(register_3_q), .we(register_1_q), .oe(register_2_q), .clk(Clk_out), .din(register_4_q),
    .dout(ram_1_dout));
  Hex_Digit_Display hex_digit_display_1 (.value(ram_1_dout));  // open: dp
endmodule
