// Logisim project part2.circ as structural Verilog: 2 circuits, main circuit main
module main (
  input  Reset,
  input  EN,
  input  [6:0] in_3,
  input  [6:0] in_4
);

  wire Clk_out;
  wire [6:0] part_2_datapath_1_x_out, part_2_datapath_1_y_out;

  Clock Clk (.out(Clk_out));
  part_2_datapath part_2_datapath_1 (
    .Y(in_3), .X(in_4), .Enable(EN), .Clk(Clk_out), .Reset(Reset), .Y_out(part_2_datapath_1_y_out),
    .X_out(part_2_datapath_1_x_out));
  // RGB_Video rgb_video_1: pin names not known; wires that end beside it: Reset, Clk_out, EN, part_2_datapath_1_x_out, part_2_datapath_1_y_out, 24'hff0000
endmodule

module part_2_datapath (
  input  [6:0] Y,
  input  [6:0] X,
  input  Enable,
  input  Clk,
  input  Reset,
  output [6:0] Y_out,
  output [6:0] X_out
);

  wire nand_1_out, not_1_out;
  wire [3:0] counter_1_q, counter_2_q;
  wire [6:0] bit_extender_1_out, bit_extender_2_out, register_1_q, register_2_q;

  not not_1 (not_1_out, Enable);
  Counter #(.max('hf), .width(4)) counter_1 (
    .clr(Reset), .load(not_1_out), .up(1'b1), .clk(Clk), .D(counter_1_q), .Q(counter_1_q));  // open: count, carry
  Register #(.width(7)) register_1 (.D(X), .en(Enable), .clk(Clk), .Q(register_1_q), .clr(Reset));
  assign bit_extender_1_out = {{3{1'b0}}, counter_1_q};  // Bit_Extender bit_extender_1
  Adder #(.width(7)) adder_1 (.a(register_1_q), .b(bit_extender_1_out), .out(X_out));  // open: cin, cout
  nand nand_1 (nand_1_out, counter_1_q[0], counter_1_q[1], counter_1_q[2], counter_1_q[3]);
  Counter #(.max('hf), .width(4)) counter_2 (
    .clr(Reset), .load(nand_1_out), .up(1'b1), .clk(Clk), .D(counter_2_q), .Q(counter_2_q));  // open: count, carry
  assign bit_extender_2_out = {{3{1'b0}}, counter_2_q};  // Bit_Extender bit_extender_2
  Register #(.width(7)) register_2 (.D(Y), .en(Enable), .clk(Clk), .Q(register_2_q), .clr(Reset));
  Adder #(.width(7)) adder_2 (.a(register_2_q), .b(bit_extender_2_out), .out(Y_out));  // open: cin, cout
endmodule
