// Logisim project Lab2_part1_and_part2.circ as structural Verilog: 4 circuits, main circuit mux4to1
module Modular2to1 (
  input  SW_0,
  input  SW_1,
  input  SW_9,
  output LEDR_0
);

  mux2to1 u (.x(SW_0), .y(SW_1), .s(SW_9), .m(LEDR_0));
endmodule

module mux2to1 (
  input  x,
  input  y,
  input  s,
  output m
);

  Multiplexer #(.enable("false")) multiplexer_1 (.in0(x), .in1(y), .out(m), .sel(s));
endmodule

module mux4to1 (
  input  u,
  input  v,
  input  s0,
  input  s1,
  input  w,
  input  x,
  output m
);

  wire A_m, B_m;

  mux2to1 A (.x(u), .y(v), .s(s0), .m(A_m));
  mux2to1 B (.x(w), .y(x), .s(s0), .m(B_m));
  mux2to1 C (.x(A_m), .y(B_m), .s(s1), .m(m));
endmodule

module Modular4to1 (
  input  SW_0,
  input  SW_1,
  input  SW_9,
  input  SW_8,
  input  SW_2,
  input  SW_3,
  output LEDR_0
);

  mux4to1 u (.u(SW_0), .v(SW_1), .s0(SW_9), .s1(SW_8), .w(SW_2), .x(SW_3), .m(LEDR_0));
endmodule
