// Logisim project Lab2_part3.circ as structural Verilog: 8 circuits, main circuit main
module main (
  input  c3,
  input  c2,
  input  c1,
  input  c0
);

  wire s0_y, s1_y, s2_y, s3_y, s4_y, s5_y, s6_y;

  Segment0 s0 (.A(c3), .B(c2), .C(c1), .D(c0), .Y(s0_y));
  Segment1 s1 (.A(c3), .B(c2), .C(c1), .D(c0), .Y(s1_y));
  Segment2 s2 (.A(c3), .B(c2), .C(c1), .D(c0), .Y(s2_y));
  Segment3 s3 (.A(c3), .B(c2), .C(c1), .D(c0), .Y(s3_y));
  Segment4 s4 (.A(c3), .B(c2), .C(c1), .D(c0), .Y(s4_y));
  Segment5 s5 (.A(c3), .B(c2), .C(c1), .D(c0), .Y(s5_y));
  Segment6 s6 (.A(c3), .B(c2), .C(c1), .D(c0), .Y(s6_y));
  _7_Segment_Display Y (.g(s6_y), .f(s5_y), .a(s0_y), .b(s1_y), .e(s4_y), .d(s3_y), .c(s2_y));  // open: dp
endmodule

module Segment0 (
  input  A,
  input  B,
  input  C,
  input  D,
  output Y
);

  wire and_1_out, and_2_out, and_3_out, and_4_out, and_5_out, and_6_out, not_1_out, not_2_out, not_3_out,
       not_4_out;

  not not_1 (not_1_out, A);
  not not_2 (not_2_out, B);
  not not_3 (not_3_out, C);
  not not_4 (not_4_out, D);
  and and_1 (and_1_out, not_1_out, C);
  and and_2 (and_2_out, not_2_out, not_4_out);
  and and_3 (and_3_out, B, C);
  and and_4 (and_4_out, A, not_4_out);
  and and_5 (and_5_out, not_1_out, B, D);
  and and_6 (and_6_out, A, not_2_out, not_3_out);
  or or_1 (Y, and_1_out, and_2_out, and_3_out, and_4_out, and_5_out, and_6_out);
endmodule

module Segment1 (
  input  A,
  input  B,
  input  C,
  input  D,
  output Y
);

  wire and_1_out, and_2_out, and_3_out, and_4_out, and_5_out, not_1_out, not_2_out, not_3_out, not_4_out;

  not not_1 (not_1_out, A);
  not not_2 (not_2_out, B);
  not not_3 (not_3_out, C);
  not not_4 (not_4_out, D);
  and and_1 (and_1_out, not_1_out, not_2_out);
  and and_2 (and_2_out, not_2_out, not_4_out);
  and and_3 (and_3_out, not_1_out, not_3_out, not_4_out);
  and and_4 (and_4_out, not_1_out, C, D);
  and and_5 (and_5_out, A, not_3_out, D);
  or or_1 (Y, and_1_out, and_2_out, and_3_out, and_4_out, and_5_out);
endmodule

module Segment2 (
  input  A,
  input  B,
  input  C,
  input  D,
  output Y
);

  wire and_1_out, and_2_out, and_3_out, and_4_out, and_5_out, not_1_out, not_2_out, not_3_out;

  not not_1 (not_1_out, A);
  not not_2 (not_2_out, B);
  not not_3 (not_3_out, C);
  and and_1 (and_1_out, not_1_out, not_3_out);
  and and_2 (and_2_out, not_1_out, D);
  and and_3 (and_3_out, not_3_out, D);
  and and_4 (and_4_out, not_1_out, B);
  and and_5 (and_5_out, A, not_2_out);
  or or_1 (Y, and_1_out, and_2_out, and_3_out, and_4_out, and_5_out);
endmodule

module Segment3 (
  input  A,
  input  B,
  input  C,
  input  D,
  output Y
);

  wire and_1_out, and_2_out, and_3_out, and_4_out, and_5_out, not_1_out, not_2_out, not_3_out, not_4_out;

  not not_1 (not_1_out, A);
  not not_2 (not_2_out, B);
  not not_3 (not_3_out, C);
  not not_4 (not_4_out, D);
  and and_1 (and_1_out, not_1_out, not_2_out, not_4_out);
  and and_2 (and_2_out, not_2_out, C, D);
  and and_3 (and_3_out, B, not_3_out, D);
  and and_4 (and_4_out, B, C, not_4_out);
  and and_5 (and_5_out, A, not_3_out, not_4_out);
  or or_1 (Y, and_1_out, and_2_out, and_3_out, and_4_out, and_5_out);
endmodule

module Segment4 (
  input  A,
  input  B,
  input  C,
  input  D,
  output Y
);

  wire and_1_out, and_2_out, and_3_out, and_4_out, not_1_out, not_2_out;

  not not_1 (not_1_out, B);
  not not_2 (not_2_out, D);
  and and_1 (and_1_out, A, C);
  and and_2 (and_2_out, not_1_out, not_2_out);
  and and_3 (and_3_out, C, not_2_out);
  and and_4 (and_4_out, A, B);
  or or_1 (Y, and_1_out, and_2_out, and_3_out, and_4_out);
endmodule

module Segment5 (
  input  A,
  input  B,
  input  C,
  input  D,
  output Y
);

  wire and_1_out, and_2_out, and_3_out, and_4_out, and_5_out, not_1_out, not_2_out, not_3_out, not_4_out;

  not not_1 (not_1_out, A);
  not not_2 (not_2_out, B);
  not not_3 (not_3_out, C);
  not not_4 (not_4_out, D);
  and and_1 (and_1_out, A, not_2_out);
  and and_2 (and_2_out, A, C);
  and and_3 (and_3_out, not_3_out, not_4_out);
  and and_4 (and_4_out, B, not_4_out);
  and and_5 (and_5_out, not_1_out, B, not_3_out);
  or or_1 (Y, and_1_out, and_2_out, and_3_out, and_4_out, and_5_out);
endmodule

module Segment6 (
  input  A,
  input  B,
  input  C,
  input  D,
  output Y
);

  wire and_1_out, and_2_out, and_3_out, and_4_out, and_5_out, not_1_out, not_2_out, not_3_out, not_4_out;

  not not_1 (not_1_out, A);
  not not_2 (not_2_out, B);
  not not_3 (not_3_out, C);
  not not_4 (not_4_out, D);
  and and_1 (and_1_out, A, not_2_out);
  and and_2 (and_2_out, not_2_out, C);
  and and_3 (and_3_out, C, not_4_out);
  and and_4 (and_4_out, A, D);
  and and_5 (and_5_out, not_1_out, B, not_3_out);
  or or_1 (Y, and_1_out, and_2_out, and_3_out, and_4_out, and_5_out);
endmodule
