// Logisim project mux.circ as structural Verilog: 2 circuits, main circuit main
module main (
  input  SW_0,
  input  SW_1,
  input  SW_9,
  output LEDR_0
);

  mux2to1 u (.x(SW_0), .y(SW_1), .s(SW_9), .m(LEDR_0));
endmodule

module mux2to1 (
  input  x,
  input  y,
  input  s,
  output m
);

  Multiplexer #(.enable("false")) multiplexer_1 (.in0(x), .in1(y), .out(m), .sel(s));
endmodule
