// Logisim project Part1.circ as structural Verilog: 2 circuits, main circuit main
module main (
  input  D,
  input  Clk,
  output Q
);

  wire gateddlatch_1_qa, not_1_out;

  not not_1 (not_1_out, Clk);
  gatedDLatch gateddlatch_1 (.D(D), .CLK(Clk), .Qa(gateddlatch_1_qa));  // open: Qb
  gatedDLatch gateddlatch_2 (.D(gateddlatch_1_qa), .CLK(not_1_out), .Qa(Q));  // open: Qb
endmodule

module gatedDLatch (
  input  D,
  input  CLK,
  output Qa,
  output Qb
);

  wire nand_1_out, nand_2_out, not_1_out;

  not not_1 (not_1_out, D);
  nand nand_1 (nand_1_out, D, CLK);
  nand nand_2 (nand_2_out, CLK, not_1_out);
  nand nand_3 (Qa, nand_1_out, Qb);
  nand nand_4 (Qb, Qa, nand_2_out);

  // Notes on the sheet:
  //   S
  //   R
  //   S'
  //   R'
endmodule
