// Logisim project Part2.circ as structural Verilog: 20 circuits, main circuit main
module main (
  input  [3:0] A,
  input  [2:0] S,
  input  Clk,
  output [7:0] Y
);

  wire sevensegment_1_y0, sevensegment_1_y1, sevensegment_1_y2, sevensegment_1_y3, sevensegment_1_y4,
       sevensegment_1_y5, sevensegment_1_y6, sevensegment_2_y0, sevensegment_2_y1, sevensegment_2_y2,
       sevensegment_2_y3, sevensegment_2_y4, sevensegment_2_y5, sevensegment_2_y6, sevensegment_3_y0,
       sevensegment_3_y1, sevensegment_3_y2, sevensegment_3_y3, sevensegment_3_y4, sevensegment_3_y5,
       sevensegment_3_y6, sevensegment_4_y0, sevensegment_4_y1, sevensegment_4_y2, sevensegment_4_y3,
       sevensegment_4_y4, sevensegment_4_y5, sevensegment_4_y6;
  wire [3:0] bit_extender_1_out;
  wire [7:0] function0_s, function1_s, function2_s, function3_y, function4_y, function5_y, function6_y,
       function7_y, multiplexer_1_out;

  sevenSegment sevensegment_1 (
    .c3(A[3]), .c2(A[2]), .c1(A[1]), .c0(A[0]), .y0(sevensegment_1_y0), .y1(sevensegment_1_y1),
    .y2(sevensegment_1_y2), .y3(sevensegment_1_y3), .y4(sevensegment_1_y4), .y5(sevensegment_1_y5),
    .y6(sevensegment_1_y6));
  sevenSegment sevensegment_2 (
    .c3(bit_extender_1_out[3]), .c2(bit_extender_1_out[2]), .c1(bit_extender_1_out[1]),
    .c0(bit_extender_1_out[0]), .y0(sevensegment_2_y0), .y1(sevensegment_2_y1), .y2(sevensegment_2_y2),
    .y3(sevensegment_2_y3), .y4(sevensegment_2_y4), .y5(sevensegment_2_y5), .y6(sevensegment_2_y6));
  _7_Segment_Display u_7_segment_display_1 (
    .g(sevensegment_1_y6), .f(sevensegment_1_y5), .a(sevensegment_1_y0), .b(sevensegment_1_y1),
    .e(sevensegment_1_y4), .d(sevensegment_1_y3), .c(sevensegment_1_y2));  // open: dp
  AddOne function0 (.A(A), .S(function0_s));
  AddAandB function1 (.B(bit_extender_1_out), .A(A), .S(function1_s));
  AddAandB_2 function2 (.B(bit_extender_1_out), .A(A), .S(function2_s));  // open: C_out
  BitwiseAB function3 (.A(A), .B(bit_extender_1_out), .Y(function3_y));
  ReductionOR function4 (.A(A), .B(bit_extender_1_out), .Y(function4_y));
  leftShift function5 (.B(bit_extender_1_out), .A(A), .Y(function5_y));
  rightShift function6 (.B(bit_extender_1_out), .A(A), .Y(function6_y));
  AtimesB function7 (.B(bit_extender_1_out), .A(A), .Y(function7_y));
  _7_Segment_Display u_7_segment_display_2 (
    .g(sevensegment_2_y6), .f(sevensegment_2_y5), .a(sevensegment_2_y0), .b(sevensegment_2_y1),
    .e(sevensegment_2_y4), .d(sevensegment_2_y3), .c(sevensegment_2_y2));  // open: dp
  Multiplexer #(.enable("false"), .select(3), .width(8)) multiplexer_1 (
    .in0(function0_s), .in1(function1_s), .in2(function2_s), .in3(function3_y), .in4(function4_y),
    .in5(function5_y), .in6(function6_y), .in7(function7_y), .out(multiplexer_1_out), .sel(S));
  Register register_1 (.D(multiplexer_1_out), .en(1'b1), .clk(Clk), .Q(Y));  // open: clr
  LED y0 (.in(Y[0]));
  Bit_Extender #(.out_width(4), .\type ("zero")) bit_extender_1 (.in(Y), .out(bit_extender_1_out));
  LED y1 (.in(Y[1]));
  LED y2 (.in(Y[2]));
  LED y3 (.in(Y[3]));
  LED y4 (.in(Y[4]));
  LED y5 (.in(Y[5]));
  LED y6 (.in(Y[6]));
  sevenSegment sevensegment_3 (
    .c3(Y[7]), .c2(Y[6]), .c1(Y[5]), .c0(Y[4]), .y0(sevensegment_3_y0), .y1(sevensegment_3_y1),
    .y2(sevensegment_3_y2), .y3(sevensegment_3_y3), .y4(sevensegment_3_y4), .y5(sevensegment_3_y5),
    .y6(sevensegment_3_y6));
  sevenSegment sevensegment_4 (
    .c3(Y[3]), .c2(Y[2]), .c1(Y[1]), .c0(Y[0]), .y0(sevensegment_4_y0), .y1(sevensegment_4_y1),
    .y2(sevensegment_4_y2), .y3(sevensegment_4_y3), .y4(sevensegment_4_y4), .y5(sevensegment_4_y5),
    .y6(sevensegment_4_y6));
  LED y7 (.in(Y[7]));
  _7_Segment_Display u_7_segment_display_3 (
    .g(sevensegment_3_y6), .f(sevensegment_3_y5), .a(sevensegment_3_y0), .b(sevensegment_3_y1),
    .e(sevensegment_3_y4), .d(sevensegment_3_y3), .c(sevensegment_3_y2));  // open: dp
  _7_Segment_Display u_7_segment_display_4 (
    .g(sevensegment_4_y6), .f(sevensegment_4_y5), .a(sevensegment_4_y0), .b(sevensegment_4_y1),
    .e(sevensegment_4_y4), .d(sevensegment_4_y3), .c(sevensegment_4_y2));  // open: dp

  // Notes on the sheet:
  //   A
  //   B
endmodule

module sevenSegment (
  input  c3,
  input  c2,
  input  c1,
  input  c0,
  output y0,
  output y1,
  output y2,
  output y3,
  output y4,
  output y5,
  output y6
);

  Segment0 s0 (.A(c3), .B(c2), .C(c1), .D(c0), .Y(y0));
  Segment1 s1 (.A(c3), .B(c2), .C(c1), .D(c0), .Y(y1));
  Segment2 s2 (.A(c3), .B(c2), .C(c1), .D(c0), .Y(y2));
  Segment3 s3 (.A(c3), .B(c2), .C(c1), .D(c0), .Y(y3));
  Segment4 s4 (.A(c3), .B(c2), .C(c1), .D(c0), .Y(y4));
  Segment5 s5 (.A(c3), .B(c2), .C(c1), .D(c0), .Y(y5));
  Segment6 s6 (.A(c3), .B(c2), .C(c1), .D(c0), .Y(y6));
  _7_Segment_Display Y (.g(y6), .f(y5), .a(y0), .b(y1), .e(y4), .d(y3), .c(y2));  // open: dp
endmodule

module Segment0 (
  input  A,
  input  B,
  input  C,
  input  D,
  output Y
);

  wire and_1_out, and_2_out, and_3_out, and_4_out, and_5_out, and_6_out, not_1_out, not_2_out, not_3_out,
       not_4_out;

  not not_1 (not_1_out, A);
  not not_2 (not_2_out, B);
  not not_3 (not_3_out, C);
  not not_4 (not_4_out, D);
  and and_1 (and_1_out, not_1_out, C);
  and and_2 (and_2_out, not_2_out, not_4_out);
  and and_3 (and_3_out, B, C);
  and and_4 (and_4_out, A, not_4_out);
  and and_5 (and_5_out, not_1_out, B, D);
  and and_6 (and_6_out, A, not_2_out, not_3_out);
  or or_1 (Y, and_1_out, and_2_out, and_3_out, and_4_out, and_5_out, and_6_out);
endmodule

module Segment1 (
  input  A,
  input  B,
  input  C,
  input  D,
  output Y
);

  wire and_1_out, and_2_out, and_3_out, and_4_out, and_5_out, not_1_out, not_2_out, not_3_out, not_4_out;

  not not_1 (not_1_out, A);
  not not_2 (not_2_out, B);
  not not_3 (not_3_out, C);
  not not_4 (not_4_out, D);
  and and_1 (and_1_out, not_1_out, not_2_out);
  and and_2 (and_2_out, not_2_out, not_4_out);
  and and_3 (and_3_out, not_1_out, not_3_out, not_4_out);
  and and_4 (and_4_out, not_1_out, C, D);
  and and_5 (and_5_out, A, not_3_out, D);
  or or_1 (Y, and_1_out, and_2_out, and_3_out, and_4_out, and_5_out);
endmodule

module Segment2 (
  input  A,
  input  B,
  input  C,
  input  D,
  output Y
);

  wire and_1_out, and_2_out, and_3_out, and_4_out, and_5_out, not_1_out, not_2_out, not_3_out;

  not not_1 (not_1_out, A);
  not not_2 (not_2_out, B);
  not not_3 (not_3_out, C);
  and and_1 (and_1_out, not_1_out, not_3_out);
  and and_2 (and_2_out, not_1_out, D);
  and and_3 (and_3_out, not_3_out, D);
  and and_4 (and_4_out, not_1_out, B);
  and and_5 (and_5_out, A, not_2_out);
  or or_1 (Y, and_1_out, and_2_out, and_3_out, and_4_out, and_5_out);
endmodule

module Segment3 (
  input  A,
  input  B,
  input  C,
  input  D,
  output Y
);

  wire and_1_out, and_2_out, and_3_out, and_4_out, and_5_out, not_1_out, not_2_out, not_3_out, not_4_out;

  not not_1 (not_1_out, A);
  not not_2 (not_2_out, B);
  not not_3 (not_3_out, C);
  not not_4 (not_4_out, D);
  and and_1 (and_1_out, not_1_out, not_2_out, not_4_out);
  and and_2 (and_2_out, not_2_out, C, D);
  and and_3 (and_3_out, B, not_3_out, D);
  and and_4 (and_4_out, B, C, not_4_out);
  and and_5 (and_5_out, A, not_3_out, not_4_out);
  or or_1 (Y, and_1_out, and_2_out, and_3_out, and_4_out, and_5_out);
endmodule

module Segment4 (
  input  A,
  input  B,
  input  C,
  input  D,
  output Y
);

  wire and_1_out, and_2_out, and_3_out, and_4_out, not_1_out, not_2_out;

  not not_1 (not_1_out, B);
  not not_2 (not_2_out, D);
  and and_1 (and_1_out, A, C);
  and and_2 (and_2_out, not_1_out, not_2_out);
  and and_3 (and_3_out, C, not_2_out);
  and and_4 (and_4_out, A, B);
  or or_1 (Y, and_1_out, and_2_out, and_3_out, and_4_out);
endmodule

module Segment5 (
  input  A,
  input  B,
  input  C,
  input  D,
  output Y
);

  wire and_1_out, and_2_out, and_3_out, and_4_out, and_5_out, not_1_out, not_2_out, not_3_out, not_4_out;

  not not_1 (not_1_out, A);
  not not_2 (not_2_out, B);
  not not_3 (not_3_out, C);
  not not_4 (not_4_out, D);
  and and_1 (and_1_out, A, not_2_out);
  and and_2 (and_2_out, A, C);
  and and_3 (and_3_out, not_3_out, not_4_out);
  and and_4 (and_4_out, B, not_4_out);
  and and_5 (and_5_out, not_1_out, B, not_3_out);
  or or_1 (Y, and_1_out, and_2_out, and_3_out, and_4_out, and_5_out);
endmodule

module Segment6 (
  input  A,
  input  B,
  input  C,
  input  D,
  output Y
);

  wire and_1_out, and_2_out, and_3_out, and_4_out, and_5_out, not_1_out, not_2_out, not_3_out, not_4_out;

  not not_1 (not_1_out, A);
  not not_2 (not_2_out, B);
  not not_3 (not_3_out, C);
  not not_4 (not_4_out, D);
  and and_1 (and_1_out, A, not_2_out);
  and and_2 (and_2_out, not_2_out, C);
  and and_3 (and_3_out, C, not_4_out);
  and and_4 (and_4_out, A, D);
  and and_5 (and_5_out, not_1_out, B, not_3_out);
  or or_1 (Y, and_1_out, and_2_out, and_3_out, and_4_out, and_5_out);
endmodule

module AddOne (
  input  [3:0] A,
  output [7:0] S
);

  fourBitAdder fourbitadder_1 (.B(4'b0001), .A(A), .C_in(1'b0), .C_out(S[4]), .S(S[3:0]));

  assign S[7:5] = 3'b000;
endmodule

module fullAdder (
  input  c_in,
  input  a,
  input  b,
  output s,
  output c_out
);

  wire and_1_out, and_2_out, xor_1_out;

  xor xor_1 (xor_1_out, a, b);
  and and_1 (and_1_out, a, b);
  and and_2 (and_2_out, c_in, xor_1_out);
  xor xor_2 (s, c_in, xor_1_out);
  or or_1 (c_out, and_2_out, and_1_out);
endmodule

module fourBitAdder (
  input  [3:0] B,
  input  [3:0] A,
  input  C_in,
  output C_out,
  output [3:0] S
);

  wire fulladder_2_c_out, fulladder_3_c_out, fulladder_4_c_out;

  fullAdder fulladder_1 (.c_in(fulladder_2_c_out), .a(A[3]), .b(B[3]), .s(S[3]), .c_out(C_out));
  fullAdder fulladder_2 (.c_in(fulladder_3_c_out), .a(A[2]), .b(B[2]), .s(S[2]), .c_out(fulladder_2_c_out));
  fullAdder fulladder_3 (.c_in(fulladder_4_c_out), .a(A[1]), .b(B[1]), .s(S[1]), .c_out(fulladder_3_c_out));
  fullAdder fulladder_4 (.c_in(C_in), .a(A[0]), .b(B[0]), .s(S[0]), .c_out(fulladder_4_c_out));
endmodule

module AddAandB (
  input  [3:0] B,
  input  [3:0] A,
  output [7:0] S
);

  fourBitAdder fourbitadder_1 (.B(B), .A(A), .C_in(1'b0), .C_out(S[4]), .S(S[3:0]));

  assign S[7:5] = 3'b000;
endmodule

module AddAandB_2 (
  input  [3:0] B,
  input  [3:0] A,
  output C_out,
  output [7:0] S
);

  wire [7:0] bit_extender_1_out, bit_extender_2_out;

  assign bit_extender_1_out = {{4{1'b0}}, B};  // Bit_Extender bit_extender_1
  assign bit_extender_2_out = {{4{1'b0}}, A};  // Bit_Extender bit_extender_2
  Adder adder_1 (.a(bit_extender_1_out), .b(bit_extender_2_out), .out(S), .cin(1'b0), .cout(C_out));
endmodule

module BitwiseAB (
  input  [3:0] A,
  input  [3:0] B,
  output [7:0] Y
);

  or or_1 (Y[4], A[0], B[0]);
  or or_2 (Y[5], A[1], B[1]);
  or or_3 (Y[6], A[2], B[2]);
  or or_4 (Y[7], A[3], B[3]);
  xor xor_1 (Y[0], A[0], B[0]);
  xor xor_2 (Y[1], A[1], B[1]);
  xor xor_3 (Y[2], B[2], A[2]);
  xor xor_4 (Y[3], A[3], B[3]);
endmodule

module ReductionOR (
  input  [3:0] A,
  input  [3:0] B,
  output [7:0] Y
);

  wire or_1_out;

  or or_1 (or_1_out, A[0], A[2], A[3], A[1], B[0], B[1], B[2], B[3]);
  assign Y = {{7{1'b0}}, or_1_out};  // Bit_Extender bit_extender_1
endmodule

module AConcatB (
  input  [3:0] B,
  input  [3:0] A,
  output [7:0] Y
);


  assign Y = {A, B};
endmodule

module leftShift (
  input  [3:0] B,
  input  [3:0] A,
  output [7:0] Y
);

  wire [15:0] bit_extender_1_out, shifter_1_out;

  assign bit_extender_1_out = {{12{1'b0}}, B};  // Bit_Extender bit_extender_1
  Shifter #(.width(16)) shifter_1 (.in(bit_extender_1_out), .\dist (A), .out(shifter_1_out));
  Bit_Extender #(.in_width(16), .out_width(8), .\type ("zero")) bit_extender_2 (.in(shifter_1_out), .out(Y));
endmodule

module rightShift (
  input  [3:0] B,
  input  [3:0] A,
  output [7:0] Y
);

  wire [15:0] bit_extender_1_out, shifter_1_out;

  assign bit_extender_1_out = {{12{1'b0}}, B};  // Bit_Extender bit_extender_1
  Shifter #(.shift("ar"), .width(16)) shifter_1 (.in(bit_extender_1_out), .\dist (A), .out(shifter_1_out));
  Bit_Extender #(.in_width(16), .out_width(8), .\type ("zero")) bit_extender_2 (.in(shifter_1_out), .out(Y));
endmodule

module AtimesB (
  input  [3:0] B,
  input  [3:0] A,
  output [7:0] Y
);

  wire [7:0] bit_extender_1_out, bit_extender_2_out;

  assign bit_extender_1_out = {{4{1'b0}}, B};  // Bit_Extender bit_extender_1
  assign bit_extender_2_out = {{4{1'b0}}, A};  // Bit_Extender bit_extender_2
  Multiplier multiplier_1 (.a(bit_extender_1_out), .b(bit_extender_2_out), .out(Y));  // open: cin, cout
endmodule
