// Logisim project part3.circ as structural Verilog: 2 circuits, main circuit main
module main (
  input  [7:0] load_val,
  input  ShiftRight,
  input  load_n,
  input  clk,
  input  reset,
  input  ASR,
  output [7:0] Q
);

  wire and_1_out;

  and and_1 (and_1_out, ASR, Q[7]);
  Shifter_bit bit0 (
    .load_val(load_val[0]), .ShiftRight(ShiftRight), .load_n(load_n), .clk(clk), .reset(reset),
    .shift_in(Q[1]), .Q(Q[0]));
  Shifter_bit bit1 (
    .load_val(load_val[1]), .ShiftRight(ShiftRight), .load_n(load_n), .clk(clk), .reset(reset),
    .shift_in(Q[2]), .Q(Q[1]));
  Shifter_bit bit2 (
    .load_val(load_val[2]), .ShiftRight(ShiftRight), .load_n(load_n), .clk(clk), .reset(reset),
    .shift_in(Q[3]), .Q(Q[2]));
  Shifter_bit bit3 (
    .load_val(load_val[3]), .ShiftRight(ShiftRight), .load_n(load_n), .clk(clk), .reset(reset),
    .shift_in(Q[4]), .Q(Q[3]));
  Shifter_bit bit4 (
    .load_val(load_val[4]), .ShiftRight(ShiftRight), .load_n(load_n), .clk(clk), .reset(reset),
    .shift_in(Q[5]), .Q(Q[4]));
  Shifter_bit bit5 (
    .load_val(load_val[5]), .ShiftRight(ShiftRight), .load_n(load_n), .clk(clk), .reset(reset),
    .shift_in(Q[6]), .Q(Q[5]));
  Shifter_bit bit6 (
    .load_val(load_val[6]), .ShiftRight(ShiftRight), .load_n(load_n), .clk(clk), .reset(reset),
    .shift_in(Q[7]), .Q(Q[6]));
  Shifter_bit bit7 (
    .load_val(load_val[7]), .ShiftRight(ShiftRight), .load_n(load_n), .clk(clk), .reset(reset),
    .shift_in(and_1_out), .Q(Q[7]));
endmodule

module Shifter_bit (
  input  load_val,
  input  ShiftRight,
  input  load_n,
  input  clk,
  input  reset,
  input  shift_in,
  output Q
);

  wire multiplexer_1_out, multiplexer_2_out;

  Multiplexer #(.enable("false")) multiplexer_1 (.in0(Q), .in1(shift_in), .out(multiplexer_1_out), .sel(ShiftRight));
  Multiplexer #(.enable("false")) multiplexer_2 (
    .in0(load_val), .in1(multiplexer_1_out), .out(multiplexer_2_out), .sel(load_n));
  D_Flip_Flop d_ff_1 (.D(multiplexer_2_out), .clk(clk), .Q(Q), .reset(reset));  // open: Qn, preset
endmodule
